// Logisim project g1-2.circ as structural Verilog: 6 circuits, main circuit main
module main (
  input  [3:0] ALUOperation,
  input  [3:0] A,
  input  [3:0] B,
  input  [3:0] ALUOperation_2,
  output Zero,
  output [3:0] Result,
  output Overflow
);

  wire alu_4_bit_2_overflow, alu_4_bit_2_zero, and_1_out, and_2_out, and_3_out, clock_1_out, comparator_1_eq,
       comparator_2_eq, mips_alu_4_bit_1_p4, mips_alu_4_bit_1_p6, multiplexer_1_out, not_1_out, not_2_out,
       xnor_1_out;
  wire [3:0] alu_4_bit_2_result, mips_alu_4_bit_1_p5, random_1_out, random_2_out;

  Clock clock_1 (.out(clock_1_out));
  Random #(.width(4)) random_1 (.clk(clock_1_out), .next(multiplexer_1_out), .out(random_1_out));  // open: clr
  Random #(.width(4), .seed(1)) random_2 (
    .clk(clock_1_out), .next(multiplexer_1_out), .out(random_2_out));  // open: clr
  ALU__4_bit alu_4_bit_1 (
    .A(A), .B(B), .Result(Result), .Overflow(Overflow), .Zero(Zero), .ALUOperationl(ALUOperation));
  ALU__4_bit alu_4_bit_2 (
    .A(random_1_out), .B(random_2_out), .Result(alu_4_bit_2_result), .Overflow(alu_4_bit_2_overflow),
    .Zero(alu_4_bit_2_zero), .ALUOperationl(ALUOperation_2));
  // MIPS_ALU_4_bit mips_alu_4_bit_1: pin names not known; wires that end beside it: random_1_out, random_2_out, ALUOperation_2, mips_alu_4_bit_1_p4, mips_alu_4_bit_1_p5, mips_alu_4_bit_1_p6
  not not_1 (not_1_out, ALUOperation_2[0]);
  and and_1 (and_1_out, not_1_out, ALUOperation_2[1]);
  xnor xnor_1 (xnor_1_out, alu_4_bit_2_zero, mips_alu_4_bit_1_p4);
  and and_2 (and_2_out, xnor_1_out, comparator_1_eq);
  Comparator #(.width(4)) comparator_1 (
    .a(alu_4_bit_2_result), .b(mips_alu_4_bit_1_p5), .eq(comparator_1_eq));  // open: gt, lt
  and and_3 (and_3_out, comparator_1_eq, comparator_2_eq);
  Comparator #(.width(1)) comparator_2 (
    .a(alu_4_bit_2_overflow), .b(mips_alu_4_bit_1_p6), .eq(comparator_2_eq));  // open: gt, lt
  Multiplexer #(.enable("false")) multiplexer_1 (
    .in0(and_2_out), .in1(and_3_out), .out(multiplexer_1_out), .sel(and_1_out));
  not not_2 (not_2_out, multiplexer_1_out);
  LED led_1 (.in(not_2_out));

  // Notes on the sheet:
  //   Manual test
  //   Automatic test
  //   Black box ALU
  //   Stop generating new examples on error
  //   Only compare overflow bit on add or subtract
  //   Black = ok
  //   Red = error
endmodule

module ALU__4_bit (
  input  [3:0] ALUOperationl,
  input  [3:0] A,
  input  [3:0] B,
  output Zero,
  output [3:0] Result,
  output Overflow
);
endmodule

module Multiplexor__2_in__1_bit (
  input  Operation,
  input  A,
  input  B,
  output Result
);

  wire and_1_out, and_2_out;

  and and_1 (and_1_out, A, ~Operation);  // AND_Gate
  or or_1 (Result, and_1_out, and_2_out);
  and and_2 (and_2_out, Operation, B);
endmodule

module Multiplexor__4_in__1_bit (
  input  [1:0] Operation,
  input  A,
  input  B,
  input  C,
  input  D,
  output Result
);

  wire multiplexor_2_in_1_bit_1_result, multiplexor_2_in_1_bit_2_result;

  Multiplexor__2_in__1_bit multiplexor_2_in_1_bit_1 (
    .A(A), .B(B), .Result(multiplexor_2_in_1_bit_1_result), .Operation(Operation[0]));
  Multiplexor__2_in__1_bit multiplexor_2_in_1_bit_2 (
    .A(C), .B(D), .Result(multiplexor_2_in_1_bit_2_result), .Operation(Operation[0]));
  Multiplexor__2_in__1_bit multiplexor_2_in_1_bit_3 (
    .A(multiplexor_2_in_1_bit_1_result), .B(multiplexor_2_in_1_bit_2_result), .Result(Result),
    .Operation(Operation[1]));
endmodule

module Adder__1_bit (
  input  a,
  input  b,
  input  carryin,
  output result,
  output carryout
);

  wire and_1_out, and_2_out, and_3_out, and_4_out, and_5_out, and_6_out, and_7_out, not_1_out, not_2_out,
       not_3_out, not_4_out, not_5_out, not_6_out;

  not not_1 (not_1_out, a);
  not not_2 (not_2_out, b);
  not not_3 (not_3_out, a);
  not not_4 (not_4_out, carryin);
  not not_5 (not_5_out, b);
  not not_6 (not_6_out, carryin);
  and and_1 (and_1_out, b, carryin);
  and and_2 (and_2_out, a, carryin);
  and and_3 (and_3_out, a, b);
  and and_4 (and_4_out, not_1_out, not_2_out, carryin);
  and and_5 (and_5_out, not_3_out, b, not_4_out);
  and and_6 (and_6_out, a, not_5_out, not_6_out);
  and and_7 (and_7_out, a, b, carryin);
  or or_1 (carryout, and_1_out, and_2_out, and_3_out);
  or or_2 (result, and_4_out, and_5_out, and_6_out, and_7_out);
endmodule

module ALU__1_bit (
  input  Ainvert,
  input  Binvert,
  input  CarryIn,
  input  [1:0] Operation,
  input  a,
  input  b,
  input  less,
  output Result,
  output CarryOut
);

  wire adder_1_bit_1_result, and_1_out, multiplexor_2_in_1_bit_1_result, multiplexor_2_in_1_bit_2_result,
       not_1_out, not_2_out, or_1_out;

  Multiplexor__2_in__1_bit multiplexor_2_in_1_bit_1 (
    .A(a), .B(not_1_out), .Result(multiplexor_2_in_1_bit_1_result), .Operation(Ainvert));
  not not_1 (not_1_out, a);
  not not_2 (not_2_out, b);
  Multiplexor__2_in__1_bit multiplexor_2_in_1_bit_2 (
    .A(b), .B(not_2_out), .Result(multiplexor_2_in_1_bit_2_result), .Operation(Binvert));
  and and_1 (and_1_out, multiplexor_2_in_1_bit_1_result, multiplexor_2_in_1_bit_2_result);
  or or_1 (or_1_out, multiplexor_2_in_1_bit_1_result, multiplexor_2_in_1_bit_2_result);
  Adder__1_bit adder_1_bit_1 (
    .a(multiplexor_2_in_1_bit_1_result), .b(multiplexor_2_in_1_bit_2_result), .carryin(CarryIn),
    .result(adder_1_bit_1_result), .carryout(CarryOut));
  Multiplexor__4_in__1_bit multiplexor_4_in_1_bit_1 (
    .Operation(Operation), .A(and_1_out), .B(or_1_out), .C(adder_1_bit_1_result), .D(less), .Result(Result));
endmodule
