// Logisim project g1-3.circ as structural Verilog: 2 circuits, main circuit main
module main (
  input  [1:0] op,
  input  [31:0] in,
  input  [4:0] shamt,
  output [31:0] Result
);

  ShiftUnit shiftunit_1 (.in(in), .shamt(shamt), .op(op), .result(Result));
endmodule

module ShiftUnit (
  input  [1:0] op,
  input  [31:0] in,
  input  [4:0] shamt,
  output [31:0] result
);
endmodule
