// Logisim project g2-1_soeren.circ as structural Verilog: 1 circuit, main circuit main
module main (
  input  in_1,
  output [31:0] jal,
  output [31:0] out_3,
  output [3:0] out_4,
  output [8:0] out_5
);

  wire and_1_out, clock, mips_alu_1_p4;
  wire [4:0] multiplexer_3_out, multiplexer_4_out;
  wire [5:4] ALU_Control_p2;
  wire [12:0] Control_p2;
  wire [31:0] adder_1_p3, adder_2_p3, bit_extender_1_out, bit_extender_2_out, bit_extender_3_out,
       mips_alu_1_p2, mips_alu_1_p5, mips_ram_1_p4, multiplexer_1_out, multiplexer_2_out, multiplexer_5_out,
       multiplexer_6_out, multiplexer_8_out, multiplexer_10_out, PC_q, registerfile_1_p5, registerfile_1_p6;

  Register #(.width(32)) PC (.D(multiplexer_1_out), .Q(PC_q), .clk(clock), .clr(in_1));  // open: en
  // Adder adder_1: pin names not known; wires that end beside it: PC_q, 32'h4, adder_1_p3
  Clock clock_1 (.out(clock));
  // MIPSProgramROM mipsprogramrom_1: pin names not known; wires that end beside it: PC_q, out_3, jal, clock, Control_p2[9]
  // PLA Control: pin names not known; wires that end beside it: out_3[31:26], {Control_p2[12:7], out_5[8:6], Control_p2[3:0]}
  Multiplexer #(.width(32), .enable("false")) multiplexer_1 (
    .in0(multiplexer_2_out), .in1({adder_1_p3[31:28], out_3[25:0], 2'b00}), .out(multiplexer_1_out),
    .sel(Control_p2[12]));
  Multiplexer #(.width(32), .enable("false")) multiplexer_2 (
    .in0(multiplexer_8_out), .in1(registerfile_1_p5), .out(multiplexer_2_out), .sel(ALU_Control_p2[5]));
  assign bit_extender_1_out = {{27{1'b0}}, out_3[10:6]};  // Bit_Extender bit_extender_1
  Multiplexer #(.width(5), .enable("false")) multiplexer_3 (
    .in0(out_3[20:16]), .in1(out_3[15:11]), .out(multiplexer_3_out), .sel(Control_p2[0]));
  Multiplexer #(.width(5), .enable("false")) multiplexer_4 (
    .in0(multiplexer_3_out), .in1({5{1'b1}}), .out(multiplexer_4_out), .sel(Control_p2[11]));
  // RegisterFile registerfile_1: pin names not known; wires that end beside it: multiplexer_4_out, out_3[25:21], out_3[20:16], in_1, registerfile_1_p5, registerfile_1_p6
  assign bit_extender_2_out = {{16{1'b0}}, out_3[15:0]};  // Bit_Extender bit_extender_2
  assign bit_extender_3_out = {{16{out_3[15]}}, out_3[15:0]};  // Bit_Extender bit_extender_3
  Multiplexer #(.width(32), .enable("false")) multiplexer_5 (
    .in0(bit_extender_2_out), .in1(bit_extender_3_out), .out(multiplexer_5_out), .sel(Control_p2[10]));
  // PLA ALU_Control: pin names not known; wires that end beside it: {out_5[8:6], out_3[5:0]}, {ALU_Control_p2, out_4}
  Multiplexer #(.width(32), .enable("false")) multiplexer_6 (
    .in0(registerfile_1_p5), .in1(bit_extender_1_out), .out(multiplexer_6_out), .sel(ALU_Control_p2[4]));
  // MIPS_ALU mips_alu_1: pin names not known; wires that end beside it: multiplexer_6_out, mips_alu_1_p2, out_4, mips_alu_1_p4, mips_alu_1_p5, mips_alu_1_p5, registerfile_1_p6, Control_p2[7]
  Multiplexer #(.width(32), .enable("false")) multiplexer_7 (
    .in0(registerfile_1_p6), .in1(multiplexer_5_out), .out(mips_alu_1_p2), .sel(Control_p2[8]));
  Multiplexer #(.width(32), .enable("false")) multiplexer_8 (
    .in0(adder_1_p3), .in1(adder_2_p3), .out(multiplexer_8_out), .sel(and_1_out));
  and and_1 (and_1_out, mips_alu_1_p4, Control_p2[1]);
  // Adder adder_2: pin names not known; wires that end beside it: adder_1_p3, {multiplexer_5_out[29:0], 2'b00}, adder_2_p3
  Multiplexer #(.width(32), .enable("false")) multiplexer_9 (
    .in0(multiplexer_10_out), .in1(multiplexer_8_out), .out(jal), .sel(Control_p2[11]));
  // MIPS_RAM mips_ram_1: pin names not known; wires that end beside it: Control_p2[2], clock, in_1, mips_ram_1_p4
  Multiplexer #(.width(32), .enable("false")) multiplexer_10 (
    .in0(mips_alu_1_p5), .in1(mips_ram_1_p4), .out(multiplexer_10_out), .sel(Control_p2[3]));

  assign out_5[5:0] = out_3[5:0];

  // Other names for the same wires on the sheet: reset = in_1

  // Notes on the sheet:
  //   10 = signExtend
  //   8 = aluSRC
  //   1 = branch
  //   7 =  memWrite
  //   2 = memRead
  //   3 = memToReg
  //   4-6 = ALUop
  //   11= jal
  //   12 = j 
  //   9 = regWrite/WriteEnable
  //   0 = regDST
  //   address
  //   rs
  //   rt
  //   rd
  //   immediate
  //   shamt
  //   funct
  //   opcode
  //   j
  //   jal
  //   jr
endmodule
