// Logisim project g3-1.circ as structural Verilog: 9 circuits, main circuit main
module main (
  input  in_1
);

  wire and_1_out, clock, id_ex_1_p11, mips_alu_1_p4, registerfile_1_p7, registerfile_1_p8, undriven;
  wire [1:0] BranchControl_p1;
  wire [4:0] ex_mem_1_rd_2, ex_mem_1_rt_2, id_ex_1_p16, id_ex_1_p19, id_ex_1_p20, mem_wb_1_rd_2,
       mem_wb_1_rt_2, multiplexer_4_out, registerfile_1_p3;
  wire [5:0] ALUControl_p2, id_ex_1_p17;
  wire [11:0] Control_p3, ex_mem_1_op_2, id_ex_1_p18, mem_wb_1_op_2;
  wire [31:0] adder_1_p3, adder_2_p3, bit_extender_1_out_3, ex_mem_1_aluresult_2, ex_mem_1_b_2, id_ex_1_p12,
       id_ex_1_p13, id_ex_1_p14, if_id_1_op_2, if_id_1_pc_4_2, mem_wb_1_aluresult_2, mem_wb_1_data_2,
       mips_alu_1_p5, mips_ram_1_p7, mipsprogramrom_1_p2, multiplexer_1_out, multiplexer_2_out,
       multiplexer_5_out, multiplexer_6_out, multiplexer_7_out, multiplexer_8_out, multiplexer_9_out, PC_q;
  wire [31:2] id_ex_1_p15;
  wire [31:30] id_ex_1_p15_2;

  Register #(.width(32)) PC (.D(multiplexer_2_out), .Q(PC_q), .clk(clock), .clr(in_1));  // open: en
  // Adder adder_1: pin names not known; wires that end beside it: 32'h4, PC_q, adder_1_p3
  Clock clock_1 (.out(clock));
  // MIPSProgramROM mipsprogramrom_1: pin names not known; wires that end beside it: PC_q, mipsprogramrom_1_p2
  IF_ID if_id_1 (
    .PC_4(adder_1_p3), .OP(mipsprogramrom_1_p2), .Disable(undriven), .Clock(clock), .PC_4_2(if_id_1_pc_4_2),
    .OP_2(if_id_1_op_2));
  // PLA BranchControl: pin names not known; wires that end beside it: BranchControl_p1
  Multiplexer #(.width(32), .enable("false")) multiplexer_1 (
    .in0(multiplexer_9_out), .in1(if_id_1_pc_4_2), .out(multiplexer_1_out), .sel(mem_wb_1_op_2[11]));
  // PLA Control: pin names not known; wires that end beside it: if_id_1_op_2[31:26], clock, Control_p3
  Multiplexer #(.width(32), .enable("false")) multiplexer_2 (
    .in0(multiplexer_8_out), .in1({if_id_1_pc_4_2[31:28], if_id_1_op_2[25:0], 2'b00}),
    .out(multiplexer_2_out), .sel(Control_p3[10]));
  // RegisterFile registerfile_1: pin names not known; wires that end beside it: multiplexer_1_out, mem_wb_1_op_2[1], registerfile_1_p3, if_id_1_op_2[25:21], if_id_1_op_2[20:16], in_1, registerfile_1_p7, registerfile_1_p8
  Multiplexer #(.width(5), .enable("false")) multiplexer_3 (
    .in0(multiplexer_4_out), .in1({5{1'b1}}), .out(registerfile_1_p3), .sel(mem_wb_1_op_2[11]));
  Bit_extender bit_extender_1 (.in_1(if_id_1_op_2[15:0]), .out_3(bit_extender_1_out_3), .in_2(Control_p3[2]));
  Multiplexer #(.width(5), .enable("false")) multiplexer_4 (
    .in0(mem_wb_1_rt_2), .in1(mem_wb_1_rd_2), .out(multiplexer_4_out), .sel(mem_wb_1_op_2[0]));
  // ID_EX id_ex_1: pin names not known; wires that end beside it: if_id_1_pc_4_2, registerfile_1_p7, registerfile_1_p8, bit_extender_1_out_3, if_id_1_op_2[10:6], if_id_1_op_2[5:0], Control_p3, if_id_1_op_2[20:16], if_id_1_op_2[15:11], clock, id_ex_1_p11, id_ex_1_p12, id_ex_1_p13, id_ex_1_p14, {id_ex_1_p15_2, id_ex_1_p15}, id_ex_1_p16, id_ex_1_p17, id_ex_1_p18, id_ex_1_p19, id_ex_1_p20
  Multiplexer #(.width(32), .enable("false")) multiplexer_5 (
    .in0(id_ex_1_p12), .in1(id_ex_1_p13), .out(multiplexer_5_out), .sel(ALUControl_p2[5]));
  Multiplexer #(.width(32), .enable("false")) multiplexer_6 (
    .in0(id_ex_1_p13), .in1({{27{1'b0}}, id_ex_1_p16}), .out(multiplexer_6_out), .sel(ALUControl_p2[4]));
  Multiplexer #(.width(32), .enable("false")) multiplexer_7 (
    .in0(id_ex_1_p14), .in1({id_ex_1_p15_2, id_ex_1_p15}), .out(multiplexer_7_out), .sel(id_ex_1_p18[6]));
  // PLA ALUControl: pin names not known; wires that end beside it: {id_ex_1_p18[5:3], id_ex_1_p17}, ALUControl_p2
  // Adder adder_2: pin names not known; wires that end beside it: multiplexer_5_out, {id_ex_1_p15, 2'b00}, adder_2_p3
  // MIPS_ALU mips_alu_1: pin names not known; wires that end beside it: multiplexer_6_out, multiplexer_7_out, ALUControl_p2[3:0], mips_alu_1_p4, mips_alu_1_p5
  Multiplexer #(.width(32), .enable("false")) multiplexer_8 (
    .in0(multiplexer_5_out), .in1(adder_2_p3), .out(multiplexer_8_out), .sel(and_1_out));
  and and_1 (and_1_out, mips_alu_1_p4, id_ex_1_p18[7]);
  EX_MEM ex_mem_1 (
    .Clock(clock), .B(id_ex_1_p14), .B_2(ex_mem_1_b_2), .ALUresult(mips_alu_1_p5),
    .ALUresult_2(ex_mem_1_aluresult_2), .OP(id_ex_1_p18), .OP_2(ex_mem_1_op_2), .rt(id_ex_1_p19),
    .rt_2(ex_mem_1_rt_2), .rd(id_ex_1_p20), .rd_2(ex_mem_1_rd_2));  // open: PC_4, Disable, PC_4_2
  // MIPS_RAM mips_ram_1: pin names not known; wires that end beside it: ex_mem_1_aluresult_2[19:0], ex_mem_1_b_2, ex_mem_1_op_2[8], ex_mem_1_op_2[9], clock, in_1, mips_ram_1_p7
  MEM_WB mem_wb_1 (
    .OP(ex_mem_1_op_2), .Clock(clock), .OP_2(mem_wb_1_op_2), .Data(mips_ram_1_p7), .Data_2(mem_wb_1_data_2),
    .ALUresult(ex_mem_1_aluresult_2), .ALUresult_2(mem_wb_1_aluresult_2), .rt(ex_mem_1_rt_2),
    .rt_2(mem_wb_1_rt_2), .rd(ex_mem_1_rd_2), .rd_2(mem_wb_1_rd_2));  // open: PC_4, Disable, PC_4_2
  Multiplexer #(.width(32), .enable("false")) multiplexer_9 (
    .in0(mem_wb_1_aluresult_2), .in1(mem_wb_1_data_2), .out(multiplexer_9_out), .sel(mem_wb_1_op_2[9]));

  // Other names for the same wires on the sheet: reset = in_1

  // Notes on the sheet:
  //   Enkeltcyklusarkitektur, vejledende løsning
  //   address
  //   rs
  //   immediate
  //   shamt
  //   funct
  //   opcode
  //   rt
  //   rd
  //   JUMP virker (husk at flushe IF)
  //   JAL virker (husk at flushe IF)
  //   RegWrite
  //   SignExt
  //   JumpLink
  //   Jump
  //   RegDst
  //   JUMPR HER
  //   JumpR
  //   ALUOp
  //   ALUSrc
  //   Shamt
  //   ALUOp
  //   Branch
  //   BEQ HER
  //   MemWrite
  //   MemRead
  //   MemRead
endmodule

module Bit_extender (
  input  [15:0] in_1,
  input  in_2,
  output [31:0] out_3
);

  wire [31:0] bit_extender_1_out, bit_extender_2_out;

  assign bit_extender_1_out = {{16{1'b0}}, in_1};  // Bit_Extender bit_extender_1
  assign bit_extender_2_out = {{16{in_1[15]}}, in_1};  // Bit_Extender bit_extender_2
  Multiplexer #(.width(32), .enable("false")) multiplexer_1 (
    .in0(bit_extender_1_out), .in1(bit_extender_2_out), .out(out_3), .sel(in_2));
endmodule

module Branch_prediction_table (
  input  [24:0] TagWrite,
  input  [1:0] PWrite,
  input  [31:0] TargetWrite,
  input  Clock,
  input  write,
  input  [4:0] IndexWrite,
  input  [4:0] Index,
  input  Clear,
  output [24:0] Tag,
  output [1:0] P,
  output [31:0] Target
);

  wire [31:27] registerfile_1_p1, registerfile_1_p7;

  // RegisterFile registerfile_1: pin names not known; wires that end beside it: {registerfile_1_p1, PWrite, TagWrite}, Clock, write, IndexWrite, Index, Clear, {registerfile_1_p7, P, Tag}
  // RegisterFile registerfile_2: pin names not known; wires that end beside it: TargetWrite, Clock, write, IndexWrite, Index, Clear, Target
endmodule

module Hazard_Detection_Unit (
  input  [31:0] IF_ID_RegisterRs,
  input  [31:0] ID_EX_RegisterRt,
  input  [31:0] IF_ID_RegisterRt,
  input  ID_EX_MemRead,
  output Stall
);

  wire comparator_1_eq, comparator_2_eq, or_1_out;

  Comparator #(.width(32)) comparator_1 (
    .a(IF_ID_RegisterRs), .b(ID_EX_RegisterRt), .eq(comparator_1_eq));  // open: gt, lt
  Comparator #(.width(32)) comparator_2 (
    .a(ID_EX_RegisterRt), .b(IF_ID_RegisterRt), .eq(comparator_2_eq));  // open: gt, lt
  or or_1 (or_1_out, comparator_1_eq, comparator_2_eq);
  and and_1 (Stall, or_1_out, ID_EX_MemRead);
endmodule

module Forwarding_unit (
  input  [31:0] ID_EX_RegisterRt,
  input  [31:0] ID_EX_RegisterRs,
  input  [31:0] EX_MEM_RegisterRd,
  input  [31:0] MEM_WB_RegisterRd,
  input  EX_MEM_RegWrite,
  input  MEM_WB_RegWrite,
  output [1:0] out_7,
  output [1:0] out_8
);

  wire and_1_out, and_2_out, comparator_1_eq, comparator_2_eq, comparator_3_eq, comparator_4_eq,
       comparator_5_eq, comparator_6_eq;

  and and_1 (and_1_out, EX_MEM_RegWrite, 1'b1);
  and and_2 (and_2_out, MEM_WB_RegWrite, 1'b1);
  Comparator #(.width(32)) comparator_1 (
    .a(ID_EX_RegisterRt), .b(EX_MEM_RegisterRd), .eq(comparator_1_eq));  // open: gt, lt
  Comparator #(.width(32)) comparator_2 (
    .a(ID_EX_RegisterRs), .b(EX_MEM_RegisterRd), .eq(comparator_2_eq));  // open: gt, lt
  Comparator #(.width(32)) comparator_3 (.a(EX_MEM_RegisterRd), .b({32{1'b0}}), .eq(comparator_3_eq));  // open: gt, lt
  Comparator #(.width(32)) comparator_4 (.a(MEM_WB_RegisterRd), .b({32{1'b0}}), .eq(comparator_4_eq));  // open: gt, lt
  Comparator #(.width(32)) comparator_5 (
    .a(MEM_WB_RegisterRd), .b(ID_EX_RegisterRt), .eq(comparator_5_eq));  // open: gt, lt
  and and_3 (out_7[1], comparator_1_eq, ~comparator_3_eq, and_1_out);  // AND_Gate
  Comparator #(.width(32)) comparator_6 (
    .a(ID_EX_RegisterRs), .b(MEM_WB_RegisterRd), .eq(comparator_6_eq));  // open: gt, lt
  and and_4 (out_8[1], comparator_2_eq, ~comparator_3_eq, and_1_out);  // AND_Gate
  and and_5 (out_7[0], comparator_5_eq, ~out_7[1], ~comparator_4_eq, and_2_out);  // AND_Gate
  and and_6 (out_8[0], comparator_6_eq, ~out_8[1], ~comparator_4_eq, and_2_out);  // AND_Gate
endmodule

module IF_ID (
  input  [31:0] PC_4,
  input  [31:0] OP,
  input  Disable,
  input  Clock,
  output [31:0] PC_4_2,
  output [31:0] OP_2
);

  wire not_1_out;

  not not_1 (not_1_out, Disable);
  Register #(.width(32), .trigger("falling")) register_1 (
    .D(PC_4), .en(not_1_out), .Q(PC_4_2), .clk(Clock));  // open: clr
  Register #(.width(32), .trigger("falling")) register_2 (.D(OP), .en(not_1_out), .Q(OP_2), .clk(Clock));  // open: clr
endmodule

module ID_EX (
  input  [31:0] PC_4,
  input  [31:0] A,
  input  [31:0] B,
  input  [31:0] imm,
  input  [4:0] shamt,
  input  [5:0] funct,
  input  [11:0] OP,
  input  [4:0] rt,
  input  [4:0] rd,
  input  Disable,
  input  Clock,
  output [31:0] PC_4_2,
  output [31:0] A_2,
  output [31:0] B_2,
  output [31:0] imm_2,
  output [4:0] shamt_2,
  output [5:0] funct_2,
  output [11:0] OP_2,
  output [4:0] rt_2,
  output [4:0] rd_2
);

  wire not_1_out;

  not not_1 (not_1_out, Disable);
  Register #(.width(32), .trigger("falling")) register_1 (
    .D(PC_4), .en(not_1_out), .Q(PC_4_2), .clk(Clock));  // open: clr
  Register #(.width(32), .trigger("falling")) register_2 (.D(A), .en(not_1_out), .Q(A_2), .clk(Clock));  // open: clr
  Register #(.width(32), .trigger("falling")) register_3 (.D(B), .en(not_1_out), .Q(B_2), .clk(Clock));  // open: clr
  Register #(.width(32), .trigger("falling")) register_4 (
    .D(imm), .en(not_1_out), .Q(imm_2), .clk(Clock));  // open: clr
  Register #(.width(5), .trigger("falling")) register_5 (
    .D(shamt), .en(not_1_out), .Q(shamt_2), .clk(Clock));  // open: clr
  Register #(.width(6), .trigger("falling")) register_6 (
    .D(funct), .en(not_1_out), .Q(funct_2), .clk(Clock));  // open: clr
  Register #(.width(12), .trigger("falling")) register_7 (.D(OP), .en(not_1_out), .Q(OP_2), .clk(Clock));  // open: clr
  Register #(.width(5), .trigger("falling")) register_8 (.D(rt), .en(not_1_out), .Q(rt_2), .clk(Clock));  // open: clr
  Register #(.width(5), .trigger("falling")) register_9 (.D(rd), .en(not_1_out), .Q(rd_2), .clk(Clock));  // open: clr
endmodule

module EX_MEM (
  input  [31:0] PC_4,
  input  [31:0] ALUresult,
  input  [31:0] B,
  input  [11:0] OP,
  input  [4:0] rt,
  input  [4:0] rd,
  input  Disable,
  input  Clock,
  output [31:0] PC_4_2,
  output [31:0] ALUresult_2,
  output [31:0] B_2,
  output [11:0] OP_2,
  output [4:0] rt_2,
  output [4:0] rd_2
);

  wire not_1_out;

  not not_1 (not_1_out, Disable);
  Register #(.width(32), .trigger("falling")) register_1 (
    .D(PC_4), .en(not_1_out), .Q(PC_4_2), .clk(Clock));  // open: clr
  Register #(.width(32), .trigger("falling")) register_2 (
    .D(ALUresult), .en(not_1_out), .Q(ALUresult_2), .clk(Clock));  // open: clr
  Register #(.width(32), .trigger("falling")) register_3 (.D(B), .en(not_1_out), .Q(B_2), .clk(Clock));  // open: clr
  Register #(.width(12), .trigger("falling")) register_4 (.D(OP), .en(not_1_out), .Q(OP_2), .clk(Clock));  // open: clr
  Register #(.width(5), .trigger("falling")) register_5 (.D(rt), .Q(rt_2), .clk(Clock));  // open: en, clr
  Register #(.width(5), .trigger("falling")) register_6 (.D(rd), .en(not_1_out), .Q(rd_2), .clk(Clock));  // open: clr
endmodule

module MEM_WB (
  input  [31:0] PC_4,
  input  [31:0] ALUresult,
  input  [31:0] Data,
  input  [11:0] OP,
  input  [4:0] rt,
  input  [4:0] rd,
  input  Disable,
  input  Clock,
  output [31:0] PC_4_2,
  output [31:0] ALUresult_2,
  output [31:0] Data_2,
  output [11:0] OP_2,
  output [4:0] rt_2,
  output [4:0] rd_2
);

  wire not_1_out;

  not not_1 (not_1_out, Disable);
  Register #(.width(32), .trigger("falling")) register_1 (
    .D(PC_4), .en(not_1_out), .Q(PC_4_2), .clk(Clock));  // open: clr
  Register #(.width(32), .trigger("falling")) register_2 (
    .D(ALUresult), .en(not_1_out), .Q(ALUresult_2), .clk(Clock));  // open: clr
  Register #(.width(32), .trigger("falling")) register_3 (
    .D(Data), .en(not_1_out), .Q(Data_2), .clk(Clock));  // open: clr
  Register #(.width(12), .trigger("falling")) register_4 (.D(OP), .en(not_1_out), .Q(OP_2), .clk(Clock));  // open: clr
  Register #(.width(5), .trigger("falling")) register_5 (.D(rt), .Q(rt_2), .clk(Clock));  // open: en, clr
  Register #(.width(5), .trigger("falling")) register_6 (.D(rd), .en(not_1_out), .Q(rd_2), .clk(Clock));  // open: clr
endmodule
